# Fritzing sketch Lego rc car v2 (saved by Fritzing 0.9.2b)
breadboards: 1

parts:
  Part1 = Arduino Uno (Rev3)
  IC1 = L293D [package=THT]
  Lego_battery_plug_9V_dark_grey_1 = DIP - 8 pins [package="DIP (Dual Inline) [THT]"]
  Part2 = Bluetooth HC-05 Macho
  R1 = Resistor [tolerance=±5% resistance=1k package=THT]
  R2 = Resistor [tolerance=±5% resistance=1k package=THT]
  R3 = Resistor [tolerance=±5% resistance=1k package=THT]
  Lego_motors_plug_light_grey_2 = DIP - 8 pins [chip_label=IC package="DIP (Dual Inline) [THT]"]
  Lego_servo_plug_light_grey_3 = DIP - 8 pins [chip_label=IC package="DIP (Dual Inline) [THT]"]

nets:
  N1: Part1.D8, IC1.In_4
  N2: Part1.D9_PWM, IC1.Enable_1
  GND: Part1.GND, IC1.0V, Lego_battery_plug_9V_dark_grey_1.GND, Part2.GND, R1.Pin_1, Lego_servo_plug_light_grey_3.GND
  N3: Part1.D0/RX, Part2.TXD
  N4: Part1.D1/TX, R3.Pin_0
  N5: Part1.D2, IC1.In_1
  N6: Part1.D3_PWM, IC1.Enable_2
  N7: Part1.D5_PWM, IC1.In_2
  N8: Part1.D6_PWM, IC1.In_3
  5V: Part1.5V, IC1.+V, Part2.VCC
  N9: IC1.Out_1_(_Controlled_by_Enable_1_), Lego_motors_plug_light_grey_2.C1
  N10: IC1.Out_2_(_Controlled_by_Enable_1_), Lego_motors_plug_light_grey_2.C2
  N11: IC1.+Vmotor, Lego_battery_plug_9V_dark_grey_1.V_lego_(9V), Lego_servo_plug_light_grey_3.V_lego_(9V)
  N12: IC1.Out_3_(_Controlled_by_Enable_2_), Lego_servo_plug_light_grey_3.C2
  N13: IC1.Out_4_(_Controlled_by_Enable_2_), Lego_servo_plug_light_grey_3.C1
  N14: Part2.RXD, R2.Pin_0, R3.Pin_1
  N15: R1.Pin_0, R2.Pin_1

custom parts:
  DIP - 8 pins: A DIP stand-in part for whatever IC you want. With 8 pins on a 300mil dual inline package (DIP) footprint.
